// Logisim project MoinAhmed_lab1.circ as structural Verilog: 1 circuit, main circuit main
module main (
  input  A,
  input  A_2,
  input  B,
  input  C,
  input  A_3,
  input  D,
  input  B_2,
  input  A_4,
  input  B_3,
  input  A_5,
  input  A_6,
  input  B_4,
  input  B_5,
  input  C_2,
  input  C_3,
  input  D_2,
  input  D_3,
  input  A_7,
  input  B_6,
  input  C_4,
  input  D_4
);

  wire AND_2_out, AND_3_out, AND_4_out, AND_5_out, And_6_out, AND_7_out, AND_8_out, AND_out, NAND_out,
       Nor_out, not_2_out, not_3_out, Not_out, OR_2_out, OR_3_out, OR_out, Xor_out;

  and AND (AND_out, A_6, B_5);
  and AND_2 (AND_2_out, C_3, D_3);
  LED A_prime (.in(Not_out));
  not Not (Not_out, A_2);
  and AND_3 (AND_3_out, A_3, B_2);
  LED L2 (.in(AND_3_out));
  or OR (OR_out, A_4, B_3);
  LED L3 (.in(OR_out));
  not not_2 (not_2_out, AND_4_out);
  and AND_4 (AND_4_out, A_7, B_6);
  and AND_5 (AND_5_out, C_4, D_4);
  not not_3 (not_3_out, AND_5_out);
  and And_6 (And_6_out, AND_out, AND_2_out);
  LED Y0 (.in(And_6_out));
  LED Y1 (.in(OR_2_out));
  or OR_2 (OR_2_out, not_2_out, not_3_out);
  nand NAND (NAND_out, A, B);
  and AND_7 (AND_7_out, C, D);
  xor Xor (Xor_out, A_5, B_4);
  nor Nor (Nor_out, C_2, D_2);
  or OR_3 (OR_3_out, NAND_out, AND_7_out);
  and AND_8 (AND_8_out, Xor_out, Nor_out);
  LED Y2 (.in(OR_3_out));
  LED Y3 (.in(AND_8_out));
endmodule
