// Logisim project MoinAhmed_lab2.circ as structural Verilog: 1 circuit, main circuit main
module main (
  input  One,
  input  Zero,
  input  C,
  input  B,
  input  A,
  input  One_2,
  input  Zero_2,
  input  C_in,
  input  B_2,
  input  A_2,
  input  C_2,
  input  B_3,
  input  A_3
);

  wire decoder_1_out1, decoder_1_out2, decoder_1_out3, decoder_1_out4, decoder_1_out5, decoder_1_out6,
       decoder_1_out7, multiplexer_1_out, multiplexer_2_out, or_1_out, or_2_out;

  Multiplexer #(.select(3)) multiplexer_1 (
    .in0(One), .in1(Zero), .in2(One), .in3(One), .in4(Zero), .in5(Zero), .in6(One), .in7(One),
    .out(multiplexer_1_out), .sel({A, B, C}));  // open: en
  LED Y0 (.in(multiplexer_1_out));
  LED Y1 (.in(multiplexer_2_out));
  Multiplexer #(.select(3)) multiplexer_2 (
    .in0(One_2), .in1(Zero_2), .in2(Zero_2), .in3(Zero_2), .in4(One_2), .in5(One_2), .in6(Zero_2),
    .in7(Zero_2), .out(multiplexer_2_out), .sel({A_3, B_3, C_2}));  // open: en
  Decoder #(.select(3)) decoder_1 (
    .out1(decoder_1_out1), .out2(decoder_1_out2), .out3(decoder_1_out3), .out4(decoder_1_out4),
    .out5(decoder_1_out5), .out6(decoder_1_out6), .out7(decoder_1_out7), .sel({A_2, B_2, C_in}));  // open: out0, en
  or or_1 (or_1_out, decoder_1_out1, decoder_1_out2, decoder_1_out4, decoder_1_out7);
  LED Sum (.in(or_1_out));
  or or_2 (or_2_out, decoder_1_out7, decoder_1_out3, decoder_1_out5, decoder_1_out6);
  LED Cout (.in(or_2_out));
endmodule
