// Logisim project MoinAhmed_lab3.circ as structural Verilog: 1 circuit, main circuit main
module main (
  input  A,
  input  Carry_In,
  input  A3,
  input  A2,
  input  A1,
  input  A0,
  input  B3,
  input  B2,
  input  B1,
  input  B0,
  input  Carry_In_2,
  input  B,
  input  A3_2,
  input  A2_2,
  input  A1_2,
  input  A0_2,
  input  B3_2,
  input  B2_2,
  input  B1_2,
  input  B0_2,
  input  A1_3,
  input  A0_3,
  input  B1_3,
  input  B0_3
);

  wire adder_1_cout, adder_1_out, adder_2_cout, adder_2_out, adder_3_cout, adder_3_out, adder_4_cout,
       adder_4_out, adder_5_cout, adder_5_out, adder_6_cout, adder_6_out, adder_7_cout, adder_7_out,
       adder_8_cout, adder_8_out, adder_9_cout, adder_9_out, adder_10_cout, adder_10_out, adder_11_cout,
       adder_11_out, adder_12_cout, adder_12_out, adder_13_cout, adder_13_out, adder_14_cout, adder_14_out,
       adder_15_out, and_1_out, and_2_out, B0_prime_2_out, B0_prime_out, B1_prime_2_out, B1_prime_out,
       B2_prime_out, B3_prime_out, or_1_out, xor_1_out, xor_2_out;

  Adder #(.width(1)) adder_1 (.a(A), .b(B), .out(adder_1_out), .cin(Carry_In), .cout(adder_1_cout));
  LED Sum (.in(adder_1_out));
  LED Carry (.in(adder_1_cout));
  xor B0_prime (B0_prime_out, 1'b1, B0_2);
  xor B1_prime (B1_prime_out, 1'b1, B1_2);
  xor B2_prime (B2_prime_out, 1'b1, B2_2);
  xor B3_prime (B3_prime_out, 1'b1, B3_2);
  Adder #(.width(1)) adder_2 (.a(B0_prime_out), .b(A0_2), .out(adder_2_out), .cin(1'b1), .cout(adder_2_cout));
  Adder #(.width(1)) adder_3 (.a(B1_prime_out), .b(A1_2), .out(adder_3_out), .cin(adder_2_cout), .cout(adder_3_cout));
  Adder #(.width(1)) adder_4 (.a(B2_prime_out), .b(A2_2), .out(adder_4_out), .cin(adder_3_cout), .cout(adder_4_cout));
  Adder #(.width(1)) adder_5 (.a(B3_prime_out), .b(A3_2), .out(adder_5_out), .cin(adder_4_cout), .cout(adder_5_cout));
  LED Diff0 (.in(adder_2_out));
  LED Diff1 (.in(adder_3_out));
  LED Diff2 (.in(adder_4_out));
  LED Diff3 (.in(adder_5_out));
  LED Overflow (.in(xor_1_out));
  xor xor_1 (xor_1_out, adder_4_cout, adder_5_cout);
  Adder #(.width(1)) adder_6 (.a(B0), .b(A0), .out(adder_6_out), .cin(Carry_In_2), .cout(adder_6_cout));
  Adder #(.width(1)) adder_7 (.a(B1), .b(A1), .out(adder_7_out), .cin(adder_6_cout), .cout(adder_7_cout));
  Adder #(.width(1)) adder_8 (.a(B2), .b(A2), .out(adder_8_out), .cin(adder_7_cout), .cout(adder_8_cout));
  Adder #(.width(1)) adder_9 (.a(B3), .b(A3), .out(adder_9_out), .cin(adder_8_cout), .cout(adder_9_cout));
  and and_1 (and_1_out, adder_9_out, adder_8_out);
  and and_2 (and_2_out, adder_9_out, adder_7_out);
  xor B0_prime_2 (B0_prime_2_out, 1'b1, B0_3);
  xor B1_prime_2 (B1_prime_2_out, 1'b1, B1_3);
  or or_1 (or_1_out, and_1_out, adder_9_cout, and_2_out);
  Adder #(.width(1)) adder_10 (.a(B0_prime_2_out), .b(A0_3), .out(adder_10_out), .cin(1'b1), .cout(adder_10_cout));
  Adder #(.width(1)) adder_11 (
    .a(B1_prime_2_out), .b(A1_3), .out(adder_11_out), .cin(adder_10_cout), .cout(adder_11_cout));
  Adder #(.width(1)) adder_12 (.a(adder_6_out), .b(1'b0), .out(adder_12_out), .cout(adder_12_cout));  // open: cin
  Adder #(.width(1)) adder_13 (
    .a(adder_7_out), .b(or_1_out), .out(adder_13_out), .cin(adder_12_cout), .cout(adder_13_cout));
  Adder #(.width(1)) adder_14 (
    .a(adder_8_out), .b(or_1_out), .out(adder_14_out), .cin(adder_13_cout), .cout(adder_14_cout));
  Adder #(.width(1)) adder_15 (.a(adder_9_out), .b(1'b0), .out(adder_15_out), .cin(adder_14_cout));  // open: cout
  LED Diff0_2 (.in(adder_10_out));
  LED Diff1_2 (.in(adder_11_out));
  xor xor_2 (xor_2_out, adder_10_cout, adder_11_cout);
  LED Overflow_2 (.in(xor_2_out));
  LED Low_0 (.in(adder_12_out));
  LED Low_1 (.in(adder_13_out));
  LED Low_2 (.in(adder_14_out));
  LED Low_3 (.in(adder_15_out));
  LED High_0 (.in(or_1_out));

  // Notes on the sheet:
  //   Part 1: 4-bit addition
  //   Part 2: 4-bit subtractor
  //   Part 3 :BCD Adder
  //   part 2 (bonus)
endmodule
