// Logisim project MoinAhmed_lab4.circ as structural Verilog: 1 circuit, main circuit main
module main (
  input  J,
  input  D,
  input  K,
  input  Preset,
  input  Enable,
  input  Preset_2,
  input  Clear,
  input  Enable_2,
  input  Clear_2,
  input  Carry_in,
  input  B0,
  input  D0,
  input  B1,
  input  D1,
  input  B2,
  input  D2,
  input  B3,
  input  D3
);

  wire adder_1_cout, adder_1_out, adder_2_cout, adder_2_out, adder_3_cout, adder_3_out, adder_4_cout,
       adder_4_out, Clear_2_out, Clear_out, Clock_2_out, Clock_3_out, Clock_4_out, Clock_out, d_ff_1_q,
       d_ff_1_qn, d_ff_2_q, d_ff_3_q, d_ff_4_q, d_ff_5_q, d_ff_6_q, d_ff_7_q, d_ff_8_q, d_ff_9_q, j_k_ff_1_q,
       j_k_ff_1_qn, not_1_out, not_2_out, not_3_out, not_4_out, Preset_2_out, Preset_out;

  Button Clock (.out(Clock_out));
  not not_1 (not_1_out, Clear);
  Button u_Clear (.out(Clear_out));
  not not_2 (not_2_out, Preset);
  D_Flip_Flop d_ff_1 (
    .clk(Clock_out), .D(D), .Q(d_ff_1_q), .Qn(d_ff_1_qn), .preset(not_2_out), .en(Enable), .reset(not_1_out));
  LED Q (.in(d_ff_1_q));
  LED Q_prime (.in(d_ff_1_qn));
  Button Clock_2 (.out(Clock_2_out));
  Button u_Preset (.out(Preset_out));
  D_Flip_Flop d_ff_2 (.clk(Clock_2_out), .D(D0), .Q(d_ff_2_q), .preset(Preset_out), .reset(Clear_out));  // open: Qn, en
  LED Q_2 (.in(d_ff_2_q));
  D_Flip_Flop d_ff_3 (.clk(Clock_2_out), .D(D1), .Q(d_ff_3_q), .preset(Preset_out), .reset(Clear_out));  // open: Qn, en
  LED Q_3 (.in(d_ff_3_q));
  LED Q_4 (.in(d_ff_4_q));
  D_Flip_Flop d_ff_4 (.clk(Clock_2_out), .D(D2), .Q(d_ff_4_q), .preset(Preset_out), .reset(Clear_out));  // open: Qn, en
  D_Flip_Flop d_ff_5 (.clk(Clock_2_out), .D(D3), .Q(d_ff_5_q), .preset(Preset_out), .reset(Clear_out));  // open: Qn, en
  LED Q_5 (.in(d_ff_5_q));
  Button Clock_3 (.out(Clock_3_out));
  not not_3 (not_3_out, Preset_2);
  not not_4 (not_4_out, Clear_2);
  Button u_Clear_2 (.out(Clear_2_out));
  J_K_Flip_Flop j_k_ff_1 (
    .J(J), .clk(Clock_3_out), .K(K), .Q(j_k_ff_1_q), .Qn(j_k_ff_1_qn), .preset(not_3_out), .en(Enable_2),
    .reset(not_4_out));
  LED Q_6 (.in(j_k_ff_1_q));
  LED Q_prime_2 (.in(j_k_ff_1_qn));
  Button Clock_4 (.out(Clock_4_out));
  Button u_Preset_2 (.out(Preset_2_out));
  LED led_1 (.in(d_ff_6_q));
  D_Flip_Flop d_ff_6 (
    .clk(Clock_4_out), .D(adder_1_out), .Q(d_ff_6_q), .preset(Preset_2_out), .reset(Clear_2_out));  // open: Qn, en
  LED led_2 (.in(d_ff_7_q));
  D_Flip_Flop d_ff_7 (
    .clk(Clock_4_out), .D(adder_2_out), .Q(d_ff_7_q), .preset(Preset_2_out), .reset(Clear_2_out));  // open: Qn, en
  LED led_3 (.in(d_ff_8_q));
  D_Flip_Flop d_ff_8 (
    .clk(Clock_4_out), .D(adder_3_out), .Q(d_ff_8_q), .preset(Preset_2_out), .reset(Clear_2_out));  // open: Qn, en
  LED led_4 (.in(d_ff_9_q));
  D_Flip_Flop d_ff_9 (
    .clk(Clock_4_out), .D(adder_4_out), .Q(d_ff_9_q), .preset(Preset_2_out), .reset(Clear_2_out));  // open: Qn, en
  LED led_5 (.in(adder_4_cout));
  Adder #(.width(1)) adder_1 (.a(d_ff_6_q), .b(B0), .out(adder_1_out), .cin(Carry_in), .cout(adder_1_cout));
  Adder #(.width(1)) adder_2 (.a(d_ff_7_q), .b(B1), .out(adder_2_out), .cin(adder_1_cout), .cout(adder_2_cout));
  Adder #(.width(1)) adder_3 (.a(d_ff_8_q), .b(B2), .out(adder_3_out), .cin(adder_2_cout), .cout(adder_3_cout));
  Adder #(.width(1)) adder_4 (.a(d_ff_9_q), .b(B3), .out(adder_4_out), .cin(adder_3_cout), .cout(adder_4_cout));

  // Notes on the sheet:
  //   Part 1: D-Flip flop
  //   Part 3: 4-registers
  //   Part 2: Jk-Flip Flop
  //   Part 3: Extended
endmodule
